// Digital circuit tom-1.dig as structural Verilog
module tom_1 (
  input  clk,
  input  in_2,
  input  [7:0] in_3,
  input  in_4,
  input  in_5,
  input  in_6,
  input  [7:0] in_7,
  input  in_8,
  input  in_9,
  input  in_10,
  input  in_11,
  input  in_12,
  input  in_15,
  input  in_16,
  input  in_17,
  output pulse,
  output clk_2
);

  wire and_1_out, and_2_out, and_3_out, and_4_out, and_5_out, and_6_out, decoder_1_out_0, decoder_1_out_1,
       decoder_1_out_2, decoder_1_out_3, delay_1_out, delay_2_out, driver_1_out, nclk, not_1_out, not_2_out,
       not_3_out, not_4_out, not_5_out, not_7_out, npulse, nTOS_eq__eq_0_nis0, or_1_out, or_2_out, xor_1_out;
  wire [1:0] CTRL_3_p3_2;
  wire [7:0] CTRL_3_p3, D_REGISTER_q, driver_2_out, driver_2_out_2, driver_3_out, I_O_HIGH_p3, I_O_LOW_p3,
       PROGRAM_COUNTER_pc, PROGRAM_COUNTER_pc_2, pulldown_1_out, R_REGISTER_q;
  wire [15:0] CTRL_2_p3, multiplexer_1_out, TOS_HIGH_out;
  wire [15:8] pulldown_1_out_2;

  not not_1 (not_1_out, nTOS_eq__eq_0_nis0);
  and and_1 (and_1_out, not_1_out, clk_2, clk, CTRL_3_p3[7]);
  Delay delay_1 (.in(in_16), .out(delay_1_out));
  xor xor_1 (xor_1_out, in_16, and_1_out);
  Multiplexer #(.Bits(16)) multiplexer_1 (
    .sel(delay_1_out), .in_0({16{1'b0}}), .in_1({pulldown_1_out_2, pulldown_1_out}), .out(multiplexer_1_out));
  // Probe on multiplexer_1_out
  tom_1_pc PROGRAM_COUNTER (
    .clk(npulse), .\input (multiplexer_1_out), .nLOAD(xor_1_out),
    .pc({PROGRAM_COUNTER_pc_2, PROGRAM_COUNTER_pc}));
  // tom_1_ctrl CTRL: pin names not known; wires that end beside it: npulse, PROGRAM_COUNTER_pc, CTRL_2_p3[7:0]
  // tom_1_ctrl CTRL_2: pin names not known; wires that end beside it: npulse, PROGRAM_COUNTER_pc_2, CTRL_2_p3[15:8]
  // Probe PC on CTRL_2_p3
  assign driver_1_out = in_17 ? npulse : 1'bz;  // Driver driver_1
  Break break_1 (.brk(driver_1_out));
  PullDown #(.Bits(16)) pulldown_1 (.out({pulldown_1_out_2, pulldown_1_out}));
  EEPROM #(.AddrBits(16), .Bits(16)) ROM (
    .A(CTRL_2_p3), .CS(1'b1), .WE(1'b0), .OE(in_16), .D({pulldown_1_out_2, pulldown_1_out}));
  // Probe ROM on {pulldown_1_out_2, pulldown_1_out}
  SixteenSeg sixteenseg_1 (.led({pulldown_1_out_2, pulldown_1_out}), .dp(in_2));
  Delay #(.delayTime(4)) delay_2 (.in(nclk), .out(delay_2_out));
  assign {driver_2_out_2, driver_2_out} = decoder_1_out_0 ? {pulldown_1_out_2, pulldown_1_out} : 16'bz;  // Driver driver_2
  // tom_1_ctrl CTRL_3: pin names not known; wires that end beside it: delay_2_out, pulldown_1_out, {CTRL_3_p3[7], CTRL_3_p3_2, CTRL_3_p3[4:0]}
  Break BREAK_2 (.brk(CTRL_3_p3[7]));
  // Probe CTRL on {CTRL_3_p3[7], CTRL_3_p3_2, CTRL_3_p3[4:0]}
  Decoder #(.Selector_Bits(2)) decoder_1 (
    .sel(CTRL_3_p3_2), .out_0(decoder_1_out_0), .out_1(decoder_1_out_1), .out_2(decoder_1_out_2),
    .out_3(decoder_1_out_3));
  or or_1 (or_1_out, CTRL_3_p3[4], decoder_1_out_1);
  and and_2 (and_2_out, nclk, clk);
  and and_3 (and_3_out, or_1_out, clk_2, clk);
  not not_2 (not_2_out, CTRL_3_p3[2]);
  // Probe tos_bus on {driver_2_out_2, driver_2_out}
  not not_3 (not_3_out, CTRL_3_p3[1]);
  not not_4 (not_4_out, CTRL_3_p3[0]);
  or or_2 (or_2_out, and_2_out, and_3_out);
  tom_1_273 TOS_LOW (.nCLR(in_16), .DATA(driver_2_out), .CLK(nclk), .OUT(TOS_HIGH_out[7:0]));
  tom_1_273 TOS_HIGH (.nCLR(in_16), .DATA(driver_2_out_2), .CLK(nclk), .OUT(TOS_HIGH_out[15:8]));
  tom_1_d_r D_REGISTER (
    .nENP(in_6), .nCCLR(in_16), .RCK(clk), .R_nC(CTRL_3_p3[4]), .nG(not_4_out), .nLOAD(in_15), .nENT(in_5),
    .U_nD(CTRL_3_p3[2]), .D(in_3), .CCK(or_2_out), .Q(D_REGISTER_q));
  tom_1_d_r R_REGISTER (
    .nENP(in_12), .nCCLR(in_16), .RCK(in_10), .R_nC(in_9), .nG(not_3_out), .nLOAD(in_11), .nENT(in_8),
    .U_nD(not_2_out), .D(in_7), .CCK(npulse), .Q(R_REGISTER_q));
  not not_5 (not_5_out, CTRL_3_p3[3]);
  and and_4 (and_4_out, clk_2, decoder_1_out_3);
  and and_5 (and_5_out, clk_2, decoder_1_out_2);
  not not_6 (npulse, clk);
  // Probe d on D_REGISTER_q
  // Probe r on R_REGISTER_q
  LED led_1 (.in(npulse));
  // Probe on npulse
  LED led_2 (.in(clk));
  tom_1_is0 nTOS_eq__eq_0 (.\input (TOS_HIGH_out), .nis0(nTOS_eq__eq_0_nis0));
  assign driver_3_out = 1'b1 ? D_REGISTER_q : 8'bz;  // Driver driver_3
  Driver #(.Bits(8)) driver_4 (.in(R_REGISTER_q), .en(1'b1));  // open: out
  D_FF d_ff_1 (.D(clk_2), .C(npulse), .Q(nclk), .nQ(clk_2));
  // Probe TOS on TOS_HIGH_out
  LED led_3 (.in(nTOS_eq__eq_0_nis0));
  not not_7 (not_7_out, CTRL_3_p3[3]);
  LED led_4 (.in(clk_2));
  LED led_5 (.in(nclk));
  // tom_1_io I_O_LOW: pin names not known; wires that end beside it: TOS_HIGH_out[7:0], not_7_out, I_O_LOW_p3
  // tom_1_io I_O_HIGH: pin names not known; wires that end beside it: TOS_HIGH_out[15:8], not_7_out, I_O_HIGH_p3
  // Probe stack addr on {in_4, driver_3_out}
  RAMSinglePortSel #(.AddrBits(9), .Bits(16)) STACK (
    .A({in_4, driver_3_out}), .CS(1'b1), .WE(CTRL_3_p3[3]), .OE(not_5_out), .D({I_O_HIGH_p3, I_O_LOW_p3}));
  and and_6 (and_6_out, decoder_1_out_1, nclk);
  RAMSinglePortSel #(.AddrBits(16), .Bits(16)) ramsingleportsel_1 (
    .A(TOS_HIGH_out), .CS(1'b1), .WE(and_6_out), .OE(1'b0), .D({I_O_HIGH_p3, I_O_LOW_p3}));
  // Probe stack_bus on {I_O_HIGH_p3, I_O_LOW_p3}
  tom_1_nand NAND (
    .A(TOS_HIGH_out), .B({I_O_HIGH_p3, I_O_LOW_p3}), .enable(and_4_out), .out({driver_2_out_2, driver_2_out}));
  // tom_1_add tom_1_add_1: pin names not known; wires that end beside it: TOS_HIGH_out, {I_O_HIGH_p3, I_O_LOW_p3}, and_5_out, {driver_2_out_2, driver_2_out}

  assign pulse = clk;

  // Other names for the same wires on the sheet: clk_t = clk_2; nreset = in_16

  // Notes on the sheet:
  //   in_9: default 1
  //   in_11: default 1
  //   in_12: default 1
  //   in_15: default 1
  //   contents of ROM (hex, n*v repeats v):
  //   d,cafe,d,0,21,0,d,0,91
  //   CTRL Pins
  //   0: D enable
  //   1: R enable
  //   2: D up/down / ~R up/down~
  //   3: STACK write enable + io enable / STACK output enable
  //   4: double pulse CLK 
  //   5-6: 0=ROM, 1=RAM, 2=ADD, 3=NAND
  //   7: pc load (break)
  //   TOS
  //   Clock
endmodule
